# Fritzing sketch TIoschol (saved by Fritzing 0.9.4)
breadboards: 1

parts:
  Onderdeel1 = RFID-RC522-v2
  Onderdeel2 = Arduino Uno (Rev3)
  LCM1602_IIC1 = LCM1602 IIC [part_number="LCM1602 IIC" chip_label="LCM1602 IIC" package="DIP (Dual Inline) [THT]"]
  LCD1 = LCD screen
  J1 = Basic Servo
  S2 = Pushbutton [package="[THT]"]
  S3 = Pushbutton [package="[THT]"]
  S4 = Pushbutton [package="[THT]"]
  S5 = Pushbutton [package="[THT]"]
  R1 = Resistor [tolerance=±5% resistance=1k package="2010 [SMD]"]
  R3 = Resistor [tolerance=±5% resistance=1k package="2010 [SMD]"]
  R4 = Resistor [tolerance=±5% resistance=1k package="2010 [SMD]"]
  R5 = Resistor [tolerance=±5% resistance=1k package="2010 [SMD]"]
  J2 = Piezo Speaker

nets:
  N1: Onderdeel1.SDA, Onderdeel2.D10_PWM/SS
  N2: Onderdeel1.SCK, Onderdeel2.D13/SCK
  N3: Onderdeel1.MOSI, Onderdeel2.D11_PWM/MOSI
  N4: Onderdeel1.MISO, Onderdeel2.D12/MISO
  GND: Onderdeel1.GND, Onderdeel2.GND, LCM1602_IIC1.GND, J1.gnd, S2.Pin_3, S2.Pin_4, S3.Pin_3, S3.Pin_4, S4.Pin_3, S4.Pin_4, S5.Pin_3, S5.Pin_4, J2.pin1
  N5: Onderdeel1.RST, Onderdeel2.D9_PWM
  3.3V: Onderdeel1.3.3V, Onderdeel2.3V3
  N6: Onderdeel2.A4/SDA, LCM1602_IIC1.SDA
  N7: Onderdeel2.A5/SCL, LCM1602_IIC1.SCL
  N8: Onderdeel2.D8, S3.Pin_1, S3.Pin_2, R3.Pin_0
  N9: Onderdeel2.D3_PWM, J2.pin2
  N10: Onderdeel2.D4, J1.pulse
  N11: Onderdeel2.D5_PWM, S5.Pin_1, S5.Pin_2, R4.Pin_1
  N12: Onderdeel2.D6_PWM, S2.Pin_1, S2.Pin_2, R5.Pin_1
  N13: Onderdeel2.D7, S4.Pin_1, S4.Pin_2, R1.Pin_1
  VCC: Onderdeel2.5V, LCM1602_IIC1.VCC, J1.vcc, R1.Pin_0, R3.Pin_1, R4.Pin_0, R5.Pin_0
  VSS: LCM1602_IIC1.VSS, LCD1.VSS
  VDD: LCM1602_IIC1.VDD, LCD1.VDD
  N14: LCM1602_IIC1.V0, LCD1.V0
  N15: LCM1602_IIC1.RS, LCD1.RS
  N16: LCM1602_IIC1.RW, LCD1.R/W
  N17: LCM1602_IIC1.E, LCD1.E
  N18: LCM1602_IIC1.D0, LCD1.DB0
  N19: LCM1602_IIC1.D1, LCD1.DB1
  N20: LCM1602_IIC1.D2, LCD1.DB2
  N21: LCM1602_IIC1.D3, LCD1.DB3
  N22: LCM1602_IIC1.D4, LCD1.DB4
  N23: LCM1602_IIC1.D5, LCD1.DB5
  N24: LCM1602_IIC1.D6, LCD1.DB6
  N25: LCM1602_IIC1.D7, LCD1.DB7
  N26: LCM1602_IIC1.A, LCD1.LED+
  N27: LCM1602_IIC1.K, LCD1.LED-
  N28: LCM1602_IIC1.LED_A, LCM1602_IIC1.LED_B

custom parts:
  RFID-RC522-v2: A simple China made RFID-RC522 Reader; do check the pin labels, as this is a MFRC522 based clone.
  LCM1602 IIC: I2C-Module to use a 1602 or 2004 LCD on with the wire.h libory Serial LCD Modul
